# Fritzing sketch P-Light (saved by Fritzing 0.9.3b)
breadboards: 1

parts:
  U1 = Voltage Regulator - 5V [package="TO220 [THT]"]
  R1 = Resistor [tolerance=±1% resistance=470 package=THT]
  R2 = Resistor [tolerance=±1% resistance=470 package=THT]
  C1 = Electrolytic Capacitor [capacitance=1µF package="100 mil [THT, electrolytic]"]
  C2 = Ceramic Capacitor [capacitance=100nF package="200 mil [THT, multilayer]"]
  C3 = Tantalum Capacitor [capacitance=10µF package="200 mil [THT, tantalum]"]
  C4 = Ceramic Capacitor [capacitance=100nF package="200 mil [THT, multilayer]"]

nets:
  N1: U1.input_voltage, C1.+, C2.1
  N2: U1.GND, R1.Pin_1, R2.Pin_1
  N3: U1.output_voltage, R1.Pin_0, C3.+, C4.0
  N4: R2.Pin_0, C1.-, C2.0, C3.-, C4.1
